# Fritzing sketch ボタンとLEDシールド_ユニバーサル基板 (saved by Fritzing 0.9.3b)
perfboards: 1

parts:
  J3 = double row male pin header, 20 pins [form="♂ (male)"]
  J4 = double row male pin header, 20 pins [form="♂ (male)"]  # not connected
  R1 = Resistor [tolerance=±5% resistance=51 package=THT]
  LED1 = LED - 5mm [color="Yellow (595nm)" package="5 mm [THT]"]
  S1 = Pushbutton [package="[THT]"]

nets:
  N1: J3.pin1, S1.Pin_1, S1.Pin_2
  N2: J3.pin5, LED1.anode
  N3: J3.pin18, R1.Pin_0
  N4: J3.pin19, S1.Pin_3, S1.Pin_4
  N5: R1.Pin_1, LED1.cathode
