# Fritzing sketch ボタンとLED回路 (saved by Fritzing 1.0.2b)
breadboards: 1

parts:
  R1 = Resistor [tolerance=±5% resistance=51 power=0.25W package=THT]
  LED1 = LED - 5mm [color="Yellow (595nm)" current=0.030A package="5 mm [THT]"]
  S1 = Pushbutton [package="[THT]"]
  Raspberry_Pi_1 = Raspberry Pi 3 [part_number=RPI-3-V1.2]

nets:
  N1: R1.Pin_0, LED1.anode
  N2: R1.Pin_1, Raspberry_Pi_1.GPIO19
  N3: LED1.cathode, Raspberry_Pi_1.GND
  N4: S1.Pin_1, S1.Pin_2, Raspberry_Pi_1.3v3
  Button: S1.Pin_3, S1.Pin_4, Raspberry_Pi_1.GPIO26
